# Fritzing sketch GarminuinoPCB_v1_3 (saved by Fritzing 0.9.3b)
circuit board: 6.81331cm x 2.21919cm
breadboards: 4

parts:
  SparkFun_Pro_Micro = SparkFun Pro Micro [part_number=DEV-12640]
  DFPlayer_Mini = DFRobot DFPlayer Mini [part_number=DFR0299]
  U1 = USB Connectors [package=usb-microb]
  R1 = Resistor [tolerance=±5% resistance=1k package="0805 [SMD]"]
  VBUS = female pin header, 1 pin [form="♀ (female)"]
  R3 = Resistor [tolerance=±5% resistance=0 package="0805 [SMD]"]
  R5 = Resistor [tolerance=±5% resistance=0 package="0805 [SMD]"]
  R4 = Resistor [tolerance=±5% resistance=0 package="0805 [SMD]"]
  R2 = Resistor [tolerance=±5% resistance=0 package="0805 [SMD]"]
  HC-05_OBD = Bluetooth HC-05 Macho
  HC-05_Garmin_HUD = Bluetooth HC-05 Macho
  SPK = female pin header, 2 pins [form="♀ (female)"]

nets:
  5V: SparkFun_Pro_Micro.RAW, U1.VBUS, VBUS.pin1
  GND: SparkFun_Pro_Micro.GND, DFPlayer_Mini.GND-1, DFPlayer_Mini.GND-2, U1.GND, HC-05_OBD.GND, HC-05_Garmin_HUD.GND
  3.3V: SparkFun_Pro_Micro.VCC, DFPlayer_Mini.VCC, HC-05_OBD.VCC, HC-05_Garmin_HUD.VCC
  N1: SparkFun_Pro_Micro.A3, HC-05_OBD.State
  N2: SparkFun_Pro_Micro.A2, R4.Pin_0
  N3: SparkFun_Pro_Micro.A1, R5.Pin_0
  N4: SparkFun_Pro_Micro.A0, HC-05_Garmin_HUD.Key
  N5: SparkFun_Pro_Micro.D8, HC-05_Garmin_HUD.RXD
  N6: SparkFun_Pro_Micro.D7, HC-05_Garmin_HUD.TXD
  N7: SparkFun_Pro_Micro.D6, HC-05_Garmin_HUD.State
  N8: SparkFun_Pro_Micro.D5, R1.Pin_1
  N9: SparkFun_Pro_Micro.RXI, R3.Pin_0
  N10: SparkFun_Pro_Micro.TXO, R2.Pin_0
  N11: DFPlayer_Mini.RX, R1.Pin_0
  N12: DFPlayer_Mini.SPK_1, SPK.pin2
  N13: DFPlayer_Mini.SPK_2, SPK.pin1
  N14: R3.Pin_1, R5.Pin_1, HC-05_OBD.TXD
  N15: R4.Pin_1, R2.Pin_1, HC-05_OBD.RXD

notes:
  Garminuino v1.2
  skyforce@2018
  A2
  TX
  RX
  A1

custom parts:
  SparkFun Pro Micro: This tiny little board does all of the neat-o Arduino tricks that you’re familiar with: 4 channels of 10-bit ADC, 5 PWM pins, 12 DIOs as well as hardware serial connections Rx and Tx. Running at 16MHz and 5V, this board will remind you a lot of your other favorite Arduino-compatible boards but this little guy can go just about anywhere. There is a voltage regulator on board so it can accept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
